# Fritzing sketch Deathbot-2.0.1 (saved by Fritzing 0.9.2b)
breadboards: 1

parts:
  Part1 = Arduino Uno (Rev3) - ICSP
  J1 = Infrared Proximity Sensor  # not connected
  Q1 = NPN-Transistor [package="TO92 [THT]"]
  R1 = Resistor [tolerance=±5% resistance=220 package="2010 [SMD]"]
  U1 = SWITCH_SPDT [package=kps-1290]

nets:
  N1: Part1.5V, Q1.C, U1.P
  N2: Part1.D0/RX, Q1.B
  N3: Part1.D4, U1.S
  N4: Part1.GND, R1.Pin_1
  N5: Q1.E, R1.Pin_0
